# Fritzing sketch Vehicle_Main (saved by Fritzing 0.6.2b)
breadboards: 1

parts:
  Arduino1 = Arduino
  J1 = Basic Servo
  VCC1 = obsolete Battery
  VCC2 = obsolete Battery
  J2 = Infrared Proximity Sensor
  M1 = DC Motor  # not connected
  M2 = DC Motor  # not connected
  Part1 = XBee Explorer Regulated  # not connected

nets:
  N1: Arduino1.D11, J1.pulse
  +5V: Arduino1.+5V, J2.Vcc
  GND: Arduino1.GND, J2.GND
  N2: Arduino1.A0, J2.Vout
  N3: VCC1.+, VCC2.-
